# Fritzing sketch shreeshafritz (saved by Fritzing 0.9.3b)
breadboards: 1

parts:
  U1 = ESP8266 NodeMCU LoLin module
  R1 = Temperature Sensor (Thermistor) [thermistor_type=NTC package=THT]
  R2 = Resistor [tolerance=±5% resistance=10k package="0402 [SMD]"]
  R3 = Photocell (LDR) [package=THT]
  U2 = MLX90614 [package=to-39]
  R4 = Resistor [tolerance=±5% resistance=10k package="1206 [SMD]"]
  S1 = Toggle Switch [package=THT]
  R5 = Resistor [tolerance=±5% resistance=10k package="1206 [SMD]"]  # not connected
  R6 = Resistor [tolerance=±5% resistance=10k package="2010 [SMD]"]
  J1 = Basic Servo
  J2 = Piezo Speaker
  LED1 = LED - 3mm [color="Blue (430nm)" package="3 mm [THT]"]
  R7 = Resistor [tolerance=±5% resistance=220 package="2010 [SMD]"]
  LED2 = LED - 3mm [color="Yellow (585nm)" package="3 mm [THT]"]
  R8 = Resistor [tolerance=±5% resistance=220 package="2010 [SMD]"]

nets:
  N1: U1.D0, S1.COM, R6.Pin_0
  N2: U1.D1, R3.pin_1, R4.Pin_0
  N3: U1.D3, U2.PWM_SDA
  N4: U1.D4, U2.SCL_VZ
  3V3: U1.3V3, R1.pin_0, R3.pin_0, U2.VDD, S1.L1
  GND: U1.GND, R2.Pin_0, U2.VSS, R4.Pin_1, R6.Pin_1, J1.gnd, J2.pin1, LED1.cathode, LED2.cathode
  N5: U1.D5, R7.Pin_0
  N6: U1.D6, R8.Pin_0
  N7: U1.D7, J2.pin2
  N8: U1.D8, J1.pulse
  VIN: U1.Vin, J1.vcc
  N9: U1.A0, R1.pin_1, R2.Pin_1

custom parts:
  ESP8266 NodeMCU LoLin module: ESP8266 based NodeMCU
